// Digital circuit MIPS32SOC.dig as structural Verilog
module MIPS32SOC (
  input  clk,
  input  Reset
);

  wire aluSrc, brachEqual, brachNotEqual, Jump, memRead, memToReg, memWrite, RegDst, RegWrite;
  wire [2:0] aluFunc, aluOp;
  wire [4:0] multiplexer_2_out;
  wire [5:0] Func, Opcode;
  wire [25:6] Inst_Mem_d;
  wire [31:0] add_1_s, alu_1_res, bitextender_1_out, Data_Mem_d, multiplexer_1_out, multiplexer_3_out,
       multiplexer_4_out, PC_q, Reg_File_da, Reg_File_db;

  Multiplexer #(.Bits(32)) multiplexer_1 (.sel(Reset), .in_0(add_1_s), .in_1({32{1'b0}}), .out(multiplexer_1_out));
  Register #(.Bits(32)) PC (.D(multiplexer_1_out), .C(clk), .en(1'b1), .Q(PC_q));
  Add #(.Bits(32)) add_1 (.a(PC_q), .b(32'h4), .c_i(1'b0), .s(add_1_s));  // open: c_o
  ControlUnit controlunit_1 (
    .Opcode(Opcode), .Reset(Reset), .aluSrc(aluSrc), .RegDst(RegDst), .aluOp(aluOp), .memToReg(memToReg),
    .memRead(memRead), .memWrite(memWrite), .RegWrite(RegWrite), .branchNotEqual(brachEqual),
    .branchEqual(brachNotEqual), .Jump(Jump));
  ROM #(.AddrBits(8), .Bits(32)) Inst_Mem (.A(PC_q[9:2]), .sel(1'b1), .D({Opcode, Inst_Mem_d, Func}));
  Multiplexer #(.Bits(5)) multiplexer_2 (
    .sel(RegDst), .in_0(Inst_Mem_d[20:16]), .in_1(Inst_Mem_d[15:11]), .out(multiplexer_2_out));
  BitExtender #(.inputBits(16), .outputBits(32)) bitextender_1 (.in({Inst_Mem_d[15:6], Func}), .out(bitextender_1_out));
  RegisterFile #(.AddrBits(5), .Bits(32)) Reg_File (
    .Din(multiplexer_4_out), .we(RegWrite), .Rw(multiplexer_2_out), .C(clk), .Ra(Inst_Mem_d[25:21]),
    .Rb(Inst_Mem_d[20:16]), .Da(Reg_File_da), .Db(Reg_File_db));
  Multiplexer #(.Bits(32)) multiplexer_3 (
    .sel(aluSrc), .in_0(Reg_File_db), .in_1(bitextender_1_out), .out(multiplexer_3_out));
  ALU alu_1 (.a(Reg_File_da), .b(multiplexer_3_out), .op(aluFunc), .res(alu_1_res));  // open: isZero, lower, higher
  RAMDualPort #(.AddrBits(8), .Bits(32)) Data_Mem (
    .A(alu_1_res[9:2]), .Din(Reg_File_db), .str(memWrite), .C(clk), .ld(memRead), .D(Data_Mem_d));
  ALUControl alucontrol_1 (.aluOp(aluOp), .Func(Func), .aluFunc(aluFunc));
  Multiplexer #(.Bits(32)) multiplexer_4 (.sel(memToReg), .in_0(alu_1_res), .in_1(Data_Mem_d), .out(multiplexer_4_out));

  // Other names for the same wires on the sheet: rst = Reset

  // Notes on the sheet:
  //   contents of Inst_Mem (hex, n*v repeats v):
  //   8c080000,8c090004,ac080008
endmodule
